# Fritzing sketch esp32-sd-card-and-tft-display (saved by Fritzing 1.0.1rc)
breadboards: 1

parts:
  Part1 = node32s
  sdCard1 = my_sdCard
  Part2 = TFT 2.2 inch 320x240 w microSD [part_number=1480]

nets:
  3.3V: Part1.3.3V, Part2.VIN, Part2.BACKLIGHT
  GND: Part1.V_BATT, sdCard1.GND, Part2.GND
  5V: Part1.5V, sdCard1.VCC
  N1: Part1.IO23, Part1.IO19, Part1.IO18, Part1.IO5, sdCard1.MISO, sdCard1.MOSI, sdCard1.SCK, sdCard1.CS, Part2.MOSI, Part2.MISO, Part2.SCLK
  N2: Part1.IO4, Part2.RESET
  N3: Part1.IO2, Part2.DC

notes:
  Instead of VBATT is GND on my board
  - D/C is DC on my module
  - RST is RES on my module
  - CS and SDCS do not exist on my module
  | | | | | |
  GND VCC MISO MOSI SCK CS
  As my module has "AMS1117" regulator it uses 5V. Check yours before connecting to power rail

custom parts:
  my_sdCard: micro sdCard Adapter with 90º pin header. Use a filtering Capacitor between CS and GND if needed. PCB View Pinouts are Reversed for laying parallel on PCB using a 90º pin header.
  TFT 2.2 inch 320x240 w microSD: This lovely little display breakout is the best way to add a small, colorful and bright display to any project. Since the display uses 4-wire SPI to communicate and has its own pixel-addressable frame buffer, it can be used with every kind of microcontroller. Even a very small one with low memory and few pins available! The 2.2" display has 320x240 color pixels.
